# Fritzing sketch LCD, buzzer, SRAM, and temperature (saved by Fritzing 0.9.2b)
breadboards: 1

parts:
  C1 = Electrolytic Capacitor [capacitance=100µF voltage=50V package="100 mil [THT, electrolytic]"]
  LCD1 = LCD screen
  Part1 = Arduino Uno (Rev3)
  C2 = Electrolytic Capacitor [capacitance=1µF package="100 mil [THT, electrolytic]"]
  R1 = Trimmer Potentiometer [maximum_resistance=10kΩ package=THT]
  R2 = Resistor [tolerance=±5% resistance=220 package=THT]
  T1 = LM35 Temperature Sensor [package="TO92 [THT]"]
  IC2 = IC, DIP package, 8 pins [chip_label=23LCV512]
  J1 = Piezo Speaker

nets:
  GND: C1.-, LCD1.VSS, LCD1.R/W, LCD1.LED-, Part1.GND, C2.-, R1.leg2, T1.GND, IC2.pin4, J1.pin1
  VDD: C1.+, LCD1.VDD, Part1.5V, C2.+, R1.leg1, R2.Pin_0, T1.+Vs
  N1: LCD1.V0, R1.wiper
  N2: LCD1.RS, Part1.D9_PWM
  N3: LCD1.E, Part1.D8
  N4: LCD1.DB4, Part1.D5_PWM
  N5: LCD1.DB5, Part1.D4
  N6: LCD1.DB6, Part1.D3_PWM
  N7: LCD1.DB7, Part1.D2
  N8: LCD1.LED+, R2.Pin_1
  N9: Part1.A0, T1.Vout
  N10: Part1.D10_PWM/SS, IC2.pin1
  N11: Part1.D11_PWM/MOSI, IC2.pin5
  N12: Part1.D12/MISO, IC2.pin2
  N13: Part1.D13/SCK, IC2.pin6
  N14: Part1.D6_PWM, J1.pin2
  N15: Part1.3V3, IC2.pin8
